# Fritzing sketch LightBeacon-Node-Alpha (saved by Fritzing 0.9.3b)
circuit board: 8.46667cm x 5.64444cm

parts:
  DHT1 = DHT11 Humitidy and Temperature Sensor
  Part1 = 24 NeoPixel Ring [part_number=1586]
  U1 = NodeMCU V3.0

nets:
  VDD: DHT1.VDD, U1.3V3
  N1: DHT1.DATA, U1.D5
  GND: DHT1.GND, Part1.GND, U1.GND
  N2: Part1.IN, U1.RX
  VDD_2: Part1.VDD, U1.Vin

custom parts:
  DHT11 Humitidy and Temperature Sensor: DHT11 Humidity and Temperature Sensor
  24 NeoPixel Ring: 24 ultra bright smart LED NeoPixels are arranged in a circle with 2.6" (66mm) outer diameter. The rings are 'chainable' - connect the output pin of one to the input pin of another. Use only one microcontroller pin to control as many as you can chain together! Each LED is addressable as the driver chip is inside the LED. Each one has ~18mA constant current drive so the color will be very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
  NodeMCU V3.0: ESP8266 based NodeMCU
